// Logisim project AR.circ as structural Verilog: 1 circuit, main circuit main
module main (
  input  [11:0] INPUT,
  input  D7_prime,
  input  I,
  input  T3,
  input  T2,
  input  CLOCK,
  input  T0,
  input  D5,
  input  T4,
  output [11:0] OUTPUT
);

  wire and_1_out, and_2_out, or_1_out;

  and and_1 (and_1_out, D7_prime, I, T3);
  and and_2 (and_2_out, D5, T4);
  or or_1 (or_1_out, and_1_out, T2, T0);
  r12_LD_INR_CLR__AR_PC__main main_1 (
    .LD(or_1_out), .INC(and_2_out), .INPUT(INPUT), .CLOCK(CLOCK), .OUTPUT(OUTPUT));  // open: CLR
endmodule
