// Logisim project COMPUTER1.circ as structural Verilog: 1 circuit, main circuit main
module main (
  input  C_CLK,
  input  TR,
  input  E_IN,
  input  [15:0] in_4,
  input  E_CLR,
  input  [7:0] in_6,
  output [11:0] out_7,
  output [15:0] out_8,
  output [11:0] PC,
  output [15:0] out_10,
  output [15:0] out_11,
  output S_OUT,
  output E_OUT,
  output [7:0] OUTR
);

  wire and_1_out, and_2_out, and_3_out, and_4_out, and_5_out, and_6_out, j_k_ff_1_q, main_2_p4, main_6_p3,
       not_1_out, not_2_out, not_3_out, not_4_out, not_5_out, or_1_out, P_out, r_out;
  wire [7:0] decoder_1_out0, main_10_p3;
  wire [11:0] bit_extender_1_out, bit_extender_2_out;
  wire [15:0] main_1_p2, main_1_p4, main_12_p3, ram_1_data;

  and and_1 (and_1_out, main_1_p4[11], P_out);
  // IR_main main_1: pin names not known; wires that end beside it: out_11[1], main_1_p2, C_CLK, main_1_p4
  and and_2 (and_2_out, out_11[4], main_2_p4, decoder_1_out0[7]);
  Bit_Extender #(.in_width(16), .out_width(12)) bit_extender_1 (.in(main_1_p2), .out(bit_extender_1_out));
  not not_1 (not_1_out, decoder_1_out0[7]);
  // I_FF__main main_2: pin names not known; wires that end beside it: main_1_p4[15], C_CLK, out_11[2], main_2_p4
  not not_2 (not_2_out, main_2_p4);
  and and_3 (and_3_out, not_2_out, out_11[4], decoder_1_out0[7]);
  not not_3 (not_3_out, main_2_p4);
  and r (r_out, not_3_out, decoder_1_out0[7], out_11[3]);
  and P (P_out, main_2_p4, decoder_1_out0[7], out_11[3]);
  S_FF__main main_3 (.r(r_out), .B0(main_1_p4[0]), .CLOCK(C_CLK), .S_OUT(S_OUT));
  not not_4 (not_4_out, 1'b1);
  Decoder #(.select(3), .enable("false")) decoder_1 (
    .out0(decoder_1_out0[0]), .out1(decoder_1_out0[1]), .out2(decoder_1_out0[2]), .out3(decoder_1_out0[3]),
    .out4(decoder_1_out0[4]), .out5(decoder_1_out0[5]), .out6(decoder_1_out0[6]), .out7(decoder_1_out0[7]),
    .sel(main_1_p4[14:12]));
  SC_main main_4 (
    .D0(decoder_1_out0[0]), .T6(out_11[6]), .D1(decoder_1_out0[1]), .D2(decoder_1_out0[2]),
    .D3(decoder_1_out0[3]), .T5(out_11[5]), .D4(decoder_1_out0[4]), .D5(decoder_1_out0[5]),
    .D6(decoder_1_out0[6]), .T7(out_11[7]), .r_prime(and_3_out), .P_prime(and_2_out), .OUTPUT(out_11),
    .CLOCK(C_CLK));
  J_K_Flip_Flop j_k_ff_1 (
    .J(1'b1), .clk(C_CLK), .K(not_4_out), .Q(j_k_ff_1_q), .reset(and_1_out));  // open: Qn, preset, en
  AR_main main_5 (
    .INPUT(bit_extender_1_out), .D7_prime(not_1_out), .I(main_2_p4), .T3(out_11[3]), .T2(out_11[2]),
    .T0(out_11[0]), .D5(decoder_1_out0[5]), .T4(out_11[4]), .OUTPUT(out_7), .CLOCK(C_CLK));
  // INPR_main main_6: pin names not known; wires that end beside it: in_6, C_CLK, main_6_p3, main_1_p4[10], E_CLR
  and and_4 (and_4_out, decoder_1_out0[3], out_11[4]);
  or or_1 (or_1_out, and_4_out, and_5_out, and_6_out);
  and and_5 (and_5_out, decoder_1_out0[5], out_11[4]);
  and and_6 (and_6_out, decoder_1_out0[6], out_11[6]);
  // adder_AC_bus_main main_7: pin names not known; wires that end beside it: out_10, decoder_1_out0[0], out_11[5], decoder_1_out0[1], decoder_1_out0[2], P_out, main_1_p4[11], r_out, main_1_p4[9], main_1_p4[7], main_1_p4[6], main_1_p4[5], main_1_p4[11], r_out, main_1_p4[8], r_out, out_8, main_6_p3, C_CLK, E_IN, E_OUT
  not not_5 (not_5_out, or_1_out);
  RAM #(.addrWidth(12), .dataWidth(16)) ram_1 (
    .addr(out_7), .data(ram_1_data), .sel(1'b1), .clk(C_CLK), .ld(not_5_out));  // open: clr
  assign ram_1_data = or_1_out ? main_1_p2 : 16'bz;  // Controlled_Buffer controlled_buffer_1
  DR_main main_8 (
    .T4(out_11[4]), .D0(decoder_1_out0[0]), .D1(decoder_1_out0[1]), .D2(decoder_1_out0[2]),
    .D6(decoder_1_out0[6]), .T5(out_11[5]), .INPUT(main_1_p2), .OUTPUT(out_8), .CLOCK(C_CLK));
  PC_main main_9 (
    .D4(decoder_1_out0[4]), .T4(out_11[4]), .D5(decoder_1_out0[5]), .T5(out_11[5]), .T1(out_11[1]),
    .DR_OUT(out_8), .D6(decoder_1_out0[6]), .T6(out_11[6]), .r(r_out), .AC15(out_10[15]), .B4(main_1_p4[4]),
    .B3(main_1_p4[3]), .B2(main_1_p4[2]), .E(E_OUT), .B1(main_1_p4[1]), .P(P_out), .FGI(j_k_ff_1_q),
    .B9(main_1_p4[9]), .FGO(1'b1), .B8(main_1_p4[8]), .AC_OUT(out_10), .OUTPUT(PC), .CLOCK(C_CLK),
    .INPUT(bit_extender_2_out));
  // OUTR_main main_10: pin names not known; wires that end beside it: P_out, main_1_p4[10], main_10_p3, C_CLK, OUTR
  BUS_main main_11 (
    .AR(out_7), .PC(PC), .DR(out_8), .AC(out_10), .IR(main_1_p4), .TR(main_12_p3), .Main_MR(ram_1_data),
    .D0(decoder_1_out0[0]), .D1(decoder_1_out0[1]), .D2(decoder_1_out0[2]), .D3(decoder_1_out0[3]),
    .D4(decoder_1_out0[4]), .D5(decoder_1_out0[5]), .D6(decoder_1_out0[6]), .D7(decoder_1_out0[7]),
    .T0(out_11[0]), .T1(out_11[1]), .T2(out_11[2]), .T3(out_11[3]), .T4(out_11[4]), .T5(out_11[5]),
    .T6(out_11[6]), .T7(out_11[7]), .I(main_2_p4), .P(P_out), .B10(main_1_p4[10]), .BUS(main_1_p2));
  // TR_main main_12: pin names not known; wires that end beside it: TR, in_4, main_12_p3, C_CLK
  Bit_Extender #(.in_width(16), .out_width(12)) bit_extender_2 (.in(main_1_p2), .out(bit_extender_2_out));
  Bit_Extender #(.in_width(16), .out_width(8)) bit_extender_3 (.in(main_1_p2), .out(main_10_p3));

  // Notes on the sheet:
  //   IR
  //   I
  //   AR
  //   SC
  //   INPR
  //   AC-OUT
  //   AC
  //   AC
  //   DR
  //   BUS
endmodule
