// Logisim project DR.circ as structural Verilog: 1 circuit, main circuit main
module main (
  input  T4,
  input  D0,
  input  D1,
  input  D2,
  input  D6,
  input  CLOCK,
  input  T5,
  input  [15:0] INPUT,
  output [15:0] OUTPUT
);

  wire and_1_out, and_2_out, and_3_out, and_4_out, and_5_out, or_1_out;

  and and_1 (and_1_out, T4, D0);
  and and_2 (and_2_out, T4, D1);
  and and_3 (and_3_out, T4, D2);
  and and_4 (and_4_out, T4, D6);
  and and_5 (and_5_out, D6, T5);
  or or_1 (or_1_out, and_1_out, and_2_out, and_3_out, and_4_out);
  _16bit_reg_main main_1 (
    .load(or_1_out), .INC(and_5_out), .\input (INPUT), .CLOCK(CLOCK), .CLR(1'b0), .\output (OUTPUT));
endmodule
