// Logisim project PC.circ as structural Verilog: 1 circuit, main circuit main
module main (
  input  D4,
  input  T4,
  input  D5,
  input  T5,
  input  CLOCK,
  input  T1,
  input  [11:0] INPUT,
  input  [15:0] DR_OUT,
  input  D6,
  input  T6,
  input  r,
  input  [15:0] AC_OUT,
  input  AC15,
  input  B4,
  input  B3,
  input  B2,
  input  E,
  input  B1,
  input  P,
  input  FGI,
  input  B9,
  input  FGO,
  input  B8,
  output [11:0] OUTPUT
);

  wire and_1_out, and_2_out, and_3_out, and_4_out, and_5_out, and_6_out, and_7_out, and_8_out, and_9_out,
       and_10_out, and_11_out, not_1_out, not_2_out, not_3_out, not_4_out, not_5_out, not_6_out, not_7_out,
       not_8_out, not_9_out, not_10_out, not_11_out, not_12_out, not_13_out, not_14_out, not_15_out,
       not_16_out, not_17_out, not_18_out, not_19_out, not_20_out, not_21_out, not_22_out, not_23_out,
       not_24_out, not_25_out, not_26_out, not_27_out, not_28_out, not_29_out, not_30_out, not_31_out,
       not_32_out, not_33_out, not_34_out, not_35_out, or_1_out, or_2_out;

  not not_1 (not_1_out, AC_OUT[1]);
  not not_2 (not_2_out, AC_OUT[3]);
  not not_3 (not_3_out, AC_OUT[5]);
  not not_4 (not_4_out, AC_OUT[7]);
  not not_5 (not_5_out, AC_OUT[9]);
  not not_6 (not_6_out, AC_OUT[11]);
  not not_7 (not_7_out, AC_OUT[13]);
  not not_8 (not_8_out, AC_OUT[15]);
  not not_9 (not_9_out, DR_OUT[0]);
  not not_10 (not_10_out, DR_OUT[1]);
  not not_11 (not_11_out, DR_OUT[2]);
  not not_12 (not_12_out, DR_OUT[3]);
  not not_13 (not_13_out, DR_OUT[4]);
  not not_14 (not_14_out, DR_OUT[5]);
  not not_15 (not_15_out, DR_OUT[6]);
  not not_16 (not_16_out, DR_OUT[7]);
  not not_17 (not_17_out, DR_OUT[8]);
  not not_18 (not_18_out, DR_OUT[9]);
  not not_19 (not_19_out, DR_OUT[10]);
  not not_20 (not_20_out, DR_OUT[11]);
  not not_21 (not_21_out, DR_OUT[12]);
  not not_22 (not_22_out, DR_OUT[13]);
  not not_23 (not_23_out, DR_OUT[14]);
  not not_24 (not_24_out, DR_OUT[15]);
  not not_25 (not_25_out, AC_OUT[0]);
  not not_26 (not_26_out, AC_OUT[2]);
  not not_27 (not_27_out, AC_OUT[4]);
  not not_28 (not_28_out, AC_OUT[6]);
  not not_29 (not_29_out, AC_OUT[8]);
  not not_30 (not_30_out, AC_OUT[10]);
  not not_31 (not_31_out, AC_OUT[12]);
  not not_32 (not_32_out, AC_OUT[14]);
  and and_1 (and_1_out, not_16_out, not_9_out, not_10_out, not_11_out, not_12_out, not_13_out, not_14_out, not_15_out, not_17_out, not_18_out, not_19_out, not_20_out, not_21_out, not_22_out, not_23_out, not_24_out);
  and and_2 (and_2_out, not_4_out, not_25_out, not_1_out, not_26_out, not_2_out, not_27_out, not_3_out, not_28_out, not_29_out, not_5_out, not_30_out, not_6_out, not_31_out, not_7_out, not_32_out, not_8_out);
  not not_33 (not_33_out, AC15);
  not not_34 (not_34_out, and_2_out);
  not not_35 (not_35_out, E);
  and and_3 (and_3_out, D4, T4);
  and and_4 (and_4_out, D5, T5);
  and and_5 (and_5_out, D6, and_1_out, T6);
  and and_6 (and_6_out, r, not_33_out, B4);
  and and_7 (and_7_out, r, AC15, B3);
  and and_8 (and_8_out, r, not_34_out, B2);
  and and_9 (and_9_out, r, not_35_out, B1);
  and and_10 (and_10_out, P, FGI, B9);
  and and_11 (and_11_out, P, FGO, B8);
  or or_1 (or_1_out, and_3_out, and_4_out);
  or or_2 (or_2_out, T1, and_7_out, and_5_out, and_6_out, and_8_out, and_9_out, and_10_out, and_11_out);
  r12_LD_INR_CLR__AR_PC__main main_1 (
    .LD(or_1_out), .INC(or_2_out), .INPUT(INPUT), .CLOCK(CLOCK), .OUTPUT(OUTPUT));  // open: CLR
endmodule
