// Logisim project RAM.circ as structural Verilog: 1 circuit, main circuit main
module main (
  input  [11:0] in_1,
  input  in_2,
  input  D3,
  input  T4,
  input  D5,
  input  T4_2,
  input  D6,
  input  T6,
  output [15:0] out_9
);

  wire and_1_out, and_2_out, and_3_out, or_1_out;

  and and_1 (and_1_out, D3, T4);
  and and_2 (and_2_out, D5, T4_2);
  and and_3 (and_3_out, D6, T6);
  or or_1 (or_1_out, and_1_out, and_2_out, and_3_out);
  RAM #(.addrWidth(12), .dataWidth(16)) ram_1 (.addr(in_1), .data(out_9), .sel(in_2), .ld(or_1_out));  // open: clk, clr
endmodule
