// Logisim project S(FF).circ as structural Verilog: 1 circuit, main circuit main
module main (
  input  r,
  input  B0,
  input  CLOCK,
  output S_OUT
);

  wire and_1_out, not_1_out, not_2_out;

  and and_1 (and_1_out, r, B0);
  not not_1 (not_1_out, and_1_out);
  not not_2 (not_2_out, not_1_out);
  J_K_Flip_Flop j_k_ff_1 (.J(not_1_out), .clk(CLOCK), .K(not_2_out), .Q(S_OUT));  // open: Qn, preset, en, reset
endmodule
