// Logisim project SC.circ as structural Verilog: 1 circuit, main circuit main
module main (
  input  D0,
  input  T6,
  input  D1,
  input  CLOCK,
  input  D2,
  input  D3,
  input  T5,
  input  D4,
  input  D5,
  input  D6,
  input  T7,
  input  r_prime,
  input  P_prime,
  output [15:0] OUTPUT
);

  wire and_1_out, and_2_out, and_3_out, and_4_out, and_5_out, and_6_out, and_7_out, or_1_out;

  and and_1 (and_1_out, D0, T6);
  and and_2 (and_2_out, D1, T6);
  and and_3 (and_3_out, D2, T6);
  and and_4 (and_4_out, D3, T5);
  and and_5 (and_5_out, D4, T5);
  and and_6 (and_6_out, D5, T6);
  and and_7 (and_7_out, D6, T7);
  or or_1 (or_1_out, and_1_out, and_2_out, r_prime, and_3_out, P_prime, and_4_out, and_5_out, and_6_out, and_7_out);
  // _4bitSC_main main_1: pin names not known; wires that end beside it: CLOCK, or_1_out, OUTPUT, CLOCK
endmodule
