// Logisim project ALU.circ as structural Verilog: 1 circuit, main circuit ALU
module ALU (
  input  [2:0] F1,
  input  [2:0] F2,
  input  [2:0] F3,
  input  [15:0] from_AC,
  input  [15:0] from_DR,
  output C,
  output CLR,
  output INC,
  output B,
  output [15:0] To_AC
);

  wire [15:0] adder_1_out, and_1_out, and_2_out, and_3_out, and_4_out, and_5_out, and_6_out, and_7_out,
       and_8_out, and_9_out, and_10_out, not_1_out, or_1_out, subtractor_1_out, xor_1_out;
  wire [15:15] decoder_1_out1, decoder_1_out4, decoder_2_out1, decoder_2_out2, decoder_2_out3,
       decoder_3_out1, decoder_3_out2, decoder_3_out3, decoder_3_out4;

  Decoder #(.select(3), .enable("false")) decoder_1 (
    .out1(decoder_1_out1[15]), .out2(CLR), .out3(INC), .out4(decoder_1_out4[15]), .sel(F1));  // open: out0, out5, out6, out7
  Decoder #(.select(3), .enable("false")) decoder_2 (
    .out1(decoder_2_out1[15]), .out2(decoder_2_out2[15]), .out3(decoder_2_out3[15]), .sel(F2));  // open: out0, out4, out5, out6, out7
  Decoder #(.select(3), .enable("false")) decoder_3 (
    .out1(decoder_3_out1[15]), .out2(decoder_3_out2[15]), .out3(decoder_3_out3[15]),
    .out4(decoder_3_out4[15]), .sel(F3));  // open: out0, out5, out6, out7
  Subtractor #(.width(16)) subtractor_1 (.a(from_AC), .b(from_DR), .out(subtractor_1_out), .bin(1'b0), .bout(B));
  assign or_1_out = from_AC | from_DR;  // OR_Gate or_1, 16 bits wide
  assign and_1_out = from_DR & from_AC;  // AND_Gate and_1, 16 bits wide
  assign xor_1_out = from_AC ^ from_DR;  // XOR_Gate xor_1, 16 bits wide
  assign not_1_out = ~from_AC;  // NOT_Gate not_1, 16 bits wide
  assign and_2_out = {16{decoder_1_out4[15]}} & from_DR;  // AND_Gate and_2, 16 bits wide
  assign and_3_out = or_1_out & {16{decoder_2_out2[15]}};  // AND_Gate and_3, 16 bits wide
  assign and_4_out = and_1_out & {16{decoder_2_out3[15]}};  // AND_Gate and_4, 16 bits wide
  assign and_5_out = xor_1_out & {16{decoder_3_out1[15]}};  // AND_Gate and_5, 16 bits wide
  assign and_6_out = not_1_out & {16{decoder_3_out2[15]}};  // AND_Gate and_6, 16 bits wide
  Adder #(.width(16)) adder_1 (.a(from_AC), .b(from_DR), .out(adder_1_out), .cin(1'b0), .cout(C));
  assign and_7_out = {from_AC[14:0], from_AC[15]} & {16{decoder_3_out3[15]}};  // AND_Gate and_7, 16 bits wide
  assign and_8_out = subtractor_1_out & {16{decoder_2_out1[15]}};  // AND_Gate and_8, 16 bits wide
  assign and_9_out = {from_AC[0], from_AC[15:1]} & {16{decoder_3_out4[15]}};  // AND_Gate and_9, 16 bits wide
  assign and_10_out = adder_1_out & {16{decoder_1_out1[15]}};  // AND_Gate and_10, 16 bits wide
  assign To_AC = and_10_out | and_2_out | and_8_out | and_3_out | and_4_out | and_5_out | and_6_out | and_7_out | and_9_out;  // OR_Gate or_2, 16 bits wide
endmodule
