// Logisim project AR.circ as structural Verilog: 1 circuit, main circuit AR
module AR (
  input  [2:0] F1,
  input  [15:0] from_DR,
  input  CLOCK,
  input  [10:0] from_PC,
  output [10:0] AR_out
);

  wire or_1_out, priority_encoder_1_out;
  wire [10:0] and_1_out, and_2_out, bit_extender_1_out, multiplexer_1_out;
  wire [10:10] decoder_1_out5, decoder_1_out6;

  Decoder #(.select(3), .enable("false")) decoder_1 (
    .out5(decoder_1_out5[10]), .out6(decoder_1_out6[10]), .sel(F1));  // open: out0, out1, out2, out3, out4, out7
  or or_1 (or_1_out, decoder_1_out5[10], decoder_1_out6[10]);
  _11bit_reg_main main_1 (.LD(or_1_out), .INPUT(multiplexer_1_out), .CLOCK(CLOCK), .OUTPUT(AR_out));  // open: INC, CLR
  Bit_Extender #(.in_width(16), .out_width(11)) bit_extender_1 (.in(from_DR), .out(bit_extender_1_out));
  assign and_1_out = {11{decoder_1_out5[10]}} & bit_extender_1_out;  // AND_Gate and_1, 11 bits wide
  assign and_2_out = {11{decoder_1_out6[10]}} & from_PC;  // AND_Gate and_2, 11 bits wide
  Priority_Encoder #(.select(1)) priority_encoder_1 (
    .in0(decoder_1_out5[10]), .in1(decoder_1_out6[10]), .out(priority_encoder_1_out));  // open: gs, en_out, en_in
  Multiplexer #(.width(11), .enable("false")) multiplexer_1 (
    .in0(and_1_out), .in1(and_2_out), .out(multiplexer_1_out), .sel(priority_encoder_1_out));
endmodule
