// Logisim project DR.circ as structural Verilog: 1 circuit, main circuit DR
module DR (
  input  CLOCK,
  input  [2:0] F2,
  input  [15:0] from_RAM,
  input  [15:0] from_AC,
  input  [10:0] from_PC,
  output [15:0] DR_out
);

  wire decoder_1_out6, or_1_out;
  wire [1:0] priority_encoder_1_out;
  wire [15:0] and_1_out, and_2_out, and_3_out, bit_extender_1_out, multiplexer_1_out;
  wire [15:15] decoder_1_out4, decoder_1_out5, decoder_1_out7;

  Decoder #(.select(3), .enable("false")) decoder_1 (
    .out4(decoder_1_out4[15]), .out5(decoder_1_out5[15]), .out6(decoder_1_out6), .out7(decoder_1_out7[15]),
    .sel(F2));  // open: out0, out1, out2, out3
  or or_1 (or_1_out, decoder_1_out4[15], decoder_1_out5[15], decoder_1_out7[15]);
  assign bit_extender_1_out = {{5{1'b0}}, from_PC};  // Bit_Extender bit_extender_1
  assign and_1_out = {16{decoder_1_out4[15]}} & from_RAM;  // AND_Gate and_1, 16 bits wide
  assign and_2_out = {16{decoder_1_out5[15]}} & from_AC;  // AND_Gate and_2, 16 bits wide
  assign and_3_out = {16{decoder_1_out7[15]}} & bit_extender_1_out;  // AND_Gate and_3, 16 bits wide
  _16bit_reg_main main_1 (
    .load(or_1_out), .INC(decoder_1_out6), .\input (multiplexer_1_out), .CLOCK(CLOCK), .\output (DR_out));  // open: CLR
  Priority_Encoder #(.select(2)) priority_encoder_1 (
    .in0(1'b0), .in1(decoder_1_out5[15]), .in2(decoder_1_out4[15]), .in3(decoder_1_out7[15]),
    .out(priority_encoder_1_out));  // open: gs, en_out, en_in
  Multiplexer #(.select(2), .width(16), .enable("false")) multiplexer_1 (
    .in0({16{1'b0}}), .in1(and_2_out), .in2(and_1_out), .in3(and_3_out), .out(multiplexer_1_out),
    .sel(priority_encoder_1_out));
endmodule
