// Logisim project PC.circ as structural Verilog: 1 circuit, main circuit PC
module PC (
  input  [2:0] F3,
  input  CLOCK,
  input  [10:0] from_AR,
  output [10:0] PC_out
);

  wire decoder_1_out5;
  wire [10:0] and_1_out;
  wire [10:10] decoder_1_out6;

  Decoder #(.select(3), .enable("false")) decoder_1 (
    .out5(decoder_1_out5), .out6(decoder_1_out6[10]), .sel(F3));  // open: out0, out1, out2, out3, out4, out7
  assign and_1_out = {11{decoder_1_out6[10]}} & from_AR;  // AND_Gate and_1, 11 bits wide
  _11bit_reg_main main_1 (
    .LD(decoder_1_out6[10]), .INC(decoder_1_out5), .INPUT(and_1_out), .CLOCK(CLOCK), .OUTPUT(PC_out));  // open: CLR
endmodule
