// Logisim project computer2.circ as structural Verilog: 1 circuit, main circuit part1
module part1 (
  input  CLOCK,
  output C,
  output B,
  output [15:0] out_4
);

  wire decoder_1_out7, not_1_out;
  wire [2:0] main_1_f, main_1_f_2, main_1_f_3;
  wire [10:0] ar_1_ar_out, pc_1_pc_out;
  wire [15:0] dr_1_dr_out, ram_1_data;

  Decoder #(.select(3), .enable("false")) decoder_1 (
    .out7(decoder_1_out7), .sel(main_1_f_2));  // open: out0, out1, out2, out3, out4, out5, out6
  AR ar_1 (.F1(main_1_f_2), .from_DR(dr_1_dr_out), .from_PC(pc_1_pc_out), .AR_out(ar_1_ar_out), .CLOCK(CLOCK));
  PC pc_1 (.F3(main_1_f_3), .from_AR(ar_1_ar_out), .PC_out(pc_1_pc_out), .CLOCK(CLOCK));
  ALU_AC alu_ac_1 (
    .F1(main_1_f_2), .F2(main_1_f), .CLOCK(CLOCK), .F3(main_1_f_3), .from_DR(dr_1_dr_out), .C(C), .B(B),
    .AC_out(out_4));
  DR dr_1 (
    .F2(main_1_f), .from_RAM(ram_1_data), .from_AC(out_4), .from_PC(pc_1_pc_out), .DR_out(dr_1_dr_out),
    .CLOCK(CLOCK));
  part2_main main_1 (.CLOCK(CLOCK), .from_AC(out_4), .from_DR(dr_1_dr_out), .F({main_1_f_2, main_1_f, main_1_f_3}));
  not not_1 (not_1_out, decoder_1_out7);
  RAM #(.addrWidth(11), .dataWidth(16)) ram_1 (
    .addr(ar_1_ar_out), .data(ram_1_data), .sel(1'b1), .clk(CLOCK), .ld(not_1_out));  // open: clr
  assign ram_1_data = decoder_1_out7 ? dr_1_dr_out : 16'bz;  // Controlled_Buffer controlled_buffer_1

  // Notes on the sheet:
  //   F1
  //   F2
  //   F3
  //   AR
  //   PC
  //   AC
  //   DR
endmodule
