// Logisim project part1.circ as structural Verilog: 1 circuit, main circuit part1
module part1 (
  input  [2:0] F1,
  input  CLOCK,
  input  [2:0] F2,
  input  [2:0] F3,
  output C,
  output B
);

  wire decoder_1_out7, not_1_out;
  wire [10:0] ar_1_ar_out, pc_1_pc_out;
  wire [15:0] alu_ac_1_ac_out, dr_1_dr_out, ram_1_data;

  Decoder #(.select(3), .enable("false")) decoder_1 (
    .out7(decoder_1_out7), .sel(F1));  // open: out0, out1, out2, out3, out4, out5, out6
  AR ar_1 (.F1(F1), .from_DR(dr_1_dr_out), .from_PC(pc_1_pc_out), .AR_out(ar_1_ar_out), .CLOCK(CLOCK));
  PC pc_1 (.F3(F3), .from_AR(ar_1_ar_out), .PC_out(pc_1_pc_out), .CLOCK(CLOCK));
  ALU_AC alu_ac_1 (
    .F1(F1), .F2(F2), .CLOCK(CLOCK), .F3(F3), .from_DR(dr_1_dr_out), .C(C), .B(B), .AC_out(alu_ac_1_ac_out));
  DR dr_1 (
    .F2(F2), .from_RAM(ram_1_data), .from_AC(alu_ac_1_ac_out), .from_PC(pc_1_pc_out), .DR_out(dr_1_dr_out),
    .CLOCK(CLOCK));
  not not_1 (not_1_out, decoder_1_out7);
  RAM #(.addrWidth(11), .dataWidth(16)) ram_1 (
    .addr(ar_1_ar_out), .data(ram_1_data), .sel(1'b1), .ld(not_1_out));  // open: clk, clr
  assign ram_1_data = decoder_1_out7 ? dr_1_dr_out : 16'bz;  // Controlled_Buffer controlled_buffer_1

  // Notes on the sheet:
  //   AR
  //   PC
  //   AC
  //   DR
endmodule
