// Logisim project part2.circ as structural Verilog: 1 circuit, main circuit main
module main (
  input  CLOCK,
  input  [15:0] from_AC,
  input  [15:0] from_DR,
  output [8:0] F
);

  wire and_1_out, and_2_out, and_3_out, and_4_out, multiplexer_1_out, not_1_out, not_2_out;
  wire [1:0] or_1_out, rom_1_data;
  wire [6:0] adder_1_out, main_1_output, main_2_output, multiplexer_2_out;
  wire [7:0] rom_1_data_2;
  wire [15:0] not_3_out;

  not not_1 (not_1_out, or_1_out[1]);
  and and_1 (and_1_out, not_1_out, multiplexer_1_out);
  and and_2 (and_2_out, or_1_out[1], rom_1_data_2[7]);
  not not_2 (not_2_out, or_1_out[1]);
  or or_1 (or_1_out[0], and_1_out, and_2_out);
  and and_3 (and_3_out, not_2_out, rom_1_data_2[7], multiplexer_1_out);
  Multiplexer #(.select(2), .enable("false")) multiplexer_1 (
    .in0(1'b1), .in1(from_DR[15]), .in2(not_3_out[15]), .in3(and_4_out), .out(multiplexer_1_out),
    .sel(rom_1_data));
  assign not_3_out = ~from_AC;  // NOT_Gate not_3, 16 bits wide
  and and_4 (and_4_out, not_3_out[14], not_3_out[13], not_3_out[12], not_3_out[11], not_3_out[10], not_3_out[9], not_3_out[8], not_3_out[7], not_3_out[6], not_3_out[5], not_3_out[4], not_3_out[3], not_3_out[2], not_3_out[1], not_3_out[0]);
  Multiplexer #(.select(2), .width(7), .enable("false")) multiplexer_2 (
    .in0(adder_1_out), .in1(rom_1_data_2[6:0]), .in2(main_2_output), .in3({1'b0, from_DR[14:11], 2'b00}),
    .out(multiplexer_2_out), .sel(or_1_out));
  CAR_main main_1 (.LD(1'b1), .INPUT(multiplexer_2_out), .CLOCK(CLOCK), .OUTPUT(main_1_output));  // open: INC, CLR
  Adder #(.width(7)) adder_1 (.a(7'b0000001), .b(main_1_output), .out(adder_1_out));  // open: cin, cout
  CAR_main main_2 (.LD(and_3_out), .INPUT(adder_1_out), .CLOCK(CLOCK), .OUTPUT(main_2_output));  // open: INC, CLR
  ROM #(.addrWidth(7), .dataWidth(20)) rom_1 (
    .addr(main_1_output), .data({F, rom_1_data, or_1_out[1], rom_1_data_2}));  // open: sel

  // Notes on the sheet:
  //   S0
  //   S1
  //   L
  //   CAR
  //   SBR
  //   contents of rom_1 (hex, n*v repeats v):
  //   2c3 10002 20040 40 406 40 2c3 3040 2c3 1400a e0040 40 2c3 2000e 9400f e0040 2c3 10012 80040 40 2c3
  //   10016 4040 40 40*0 c0041 12842 a0180 10044 a0100
endmodule
