// Logisim project temp.circ as structural Verilog: 1 circuit, main circuit main
module main (
  input  [2:0] F1,
  input  [2:0] F2,
  input  [2:0] F3
);

  wire decoder_1_out7, decoder_2_out4, not_1_out;
  wire [1:0] priority_encoder_1_out;
  wire [10:0] ar_1_ar_out;
  wire [15:0] ram_1_data;

  AR ar_1 (.AR_out(ar_1_ar_out));  // open: F1, from_DR, from_PC, CLOCK
  Decoder #(.select(3), .enable("false")) decoder_1 (
    .out7(decoder_1_out7), .sel(F1));  // open: out0, out1, out2, out3, out4, out5, out6
  Decoder #(.select(3), .enable("false")) decoder_2 (
    .out4(decoder_2_out4), .sel(F2));  // open: out0, out1, out2, out3, out5, out6, out7
  Decoder #(.select(3), .enable("false")) decoder_3 (.sel(F3));  // open: out0, out1, out2, out3, out4, out5, out6, out7
  Priority_Encoder #(.select(2)) priority_encoder_1 (
    .in2(decoder_2_out4), .out(priority_encoder_1_out));  // open: in0, in1, in3, gs, en_out, en_in
  not not_1 (not_1_out, decoder_1_out7);
  RAM #(.addrWidth(11), .dataWidth(16)) ram_1 (
    .addr(ar_1_ar_out), .data(ram_1_data), .sel(1'b1), .ld(not_1_out));  // open: clk, clr
  // DR dr_1: pin names not known
endmodule
